# Fritzing sketch Single Chess set board (saved by Fritzing 0.9.2b)
breadboards: 1
stripboards: 2
perfboards: 10

parts:
  C1 = Capacitor Polarized [package=panasonic_h13]
  R1 = Resistor [tolerance=±5% resistance=220 package="0805 [SMD]"]
  J1 = Power Jack [package=power_jack_pth_lock]
  RGB_SMD_LED1 = SMD RGB LED (WS2812) [package=5050]
  S1 = Reed switch [package=THT]
  Part2 = Shift Register Breakout - 74HC595
  R2 = Resistor [tolerance=±5% resistance=220 package="0805 [SMD]"]  # not connected
  R3 = Resistor [tolerance=±5% resistance=220 package="0805 [SMD]"]  # not connected
  R4 = Resistor [tolerance=±5% resistance=220 package="0805 [SMD]"]  # not connected
  R5 = Resistor [tolerance=±5% resistance=220 package="0805 [SMD]"]  # not connected
  R6 = Resistor [tolerance=±5% resistance=220 package="0805 [SMD]"]  # not connected
  R7 = Resistor [tolerance=±5% resistance=220 package="0805 [SMD]"]  # not connected
  R8 = Resistor [tolerance=±5% resistance=220 package="0805 [SMD]"]  # not connected
  R9 = Resistor [tolerance=±5% resistance=220 package="0805 [SMD]"]  # not connected
  LCD1 = LCD screen  # not connected
  S2 = Reed switch [package=THT]
  S3 = Reed switch [package=THT]
  S4 = Reed switch [package=THT]
  S5 = Reed switch [package=THT]
  S6 = Reed switch [package=THT]
  S7 = Reed switch [package=THT]
  S8 = Reed switch [package=THT]
  S9 = Reed switch [package=THT]
  S10 = Reed switch [package=THT]
  S11 = Reed switch [package=THT]
  S12 = Reed switch [package=THT]
  S13 = Reed switch [package=THT]
  S14 = Reed switch [package=THT]
  S15 = Reed switch [package=THT]
  S16 = Reed switch [package=THT]
  S17 = Reed switch [package=THT]
  S18 = Reed switch [package=THT]
  S19 = Reed switch [package=THT]
  S20 = Reed switch [package=THT]
  S21 = Reed switch [package=THT]
  S22 = Reed switch [package=THT]
  S23 = Reed switch [package=THT]
  S24 = Reed switch [package=THT]
  S25 = Reed switch [package=THT]
  S26 = Reed switch [package=THT]
  S27 = Reed switch [package=THT]
  S28 = Reed switch [package=THT]
  S29 = Reed switch [package=THT]
  S30 = Reed switch [package=THT]
  S31 = Reed switch [package=THT]
  S32 = Reed switch [package=THT]
  S33 = Reed switch [package=THT]
  S34 = Reed switch [package=THT]
  S35 = Reed switch [package=THT]
  S36 = Reed switch [package=THT]
  S37 = Reed switch [package=THT]
  S38 = Reed switch [package=THT]
  S39 = Reed switch [package=THT]
  S40 = Reed switch [package=THT]
  S41 = Reed switch [package=THT]
  S42 = Reed switch [package=THT]
  S43 = Reed switch [package=THT]
  S44 = Reed switch [package=THT]
  S45 = Reed switch [package=THT]
  S46 = Reed switch [package=THT]
  S47 = Reed switch [package=THT]
  S48 = Reed switch [package=THT]
  S49 = Reed switch [package=THT]
  S50 = Reed switch [package=THT]
  S51 = Reed switch [package=THT]
  S52 = Reed switch [package=THT]
  S53 = Reed switch [package=THT]
  S54 = Reed switch [package=THT]
  S55 = Reed switch [package=THT]
  S56 = Reed switch [package=THT]
  S57 = Reed switch [package=THT]
  S58 = Reed switch [package=THT]
  S59 = Reed switch [package=THT]
  S60 = Reed switch [package=THT]
  S61 = Reed switch [package=THT]
  S62 = Reed switch [package=THT]
  S63 = Reed switch [package=THT]
  S64 = Reed switch [package=THT]
  Part3 = Shift Register Breakout - 74HC595
  Part4 = Shift Register Breakout - 74HC595
  Part5 = Shift Register Breakout - 74HC595
  Part6 = Shift Register Breakout - 74HC595
  Part7 = Shift Register Breakout - 74HC595
  Part8 = Shift Register Breakout - 74HC595
  Part9 = Shift Register Breakout - 74HC595
  RGB_SMD_LED2 = SMD RGB LED (WS2812) [package=5050]
  RGB_SMD_LED3 = SMD RGB LED (WS2812) [package=5050]
  RGB_SMD_LED4 = SMD RGB LED (WS2812) [package=5050]
  RGB_SMD_LED5 = SMD RGB LED (WS2812) [package=5050]
  RGB_SMD_LED7 = SMD RGB LED (WS2812) [package=5050]
  RGB_SMD_LED8 = SMD RGB LED (WS2812) [package=5050]
  RGB_SMD_LED9 = SMD RGB LED (WS2812) [package=5050]
  RGB_SMD_LED10 = SMD RGB LED (WS2812) [package=5050]
  RGB_SMD_LED11 = SMD RGB LED (WS2812) [package=5050]
  RGB_SMD_LED12 = SMD RGB LED (WS2812) [package=5050]
  RGB_SMD_LED13 = SMD RGB LED (WS2812) [package=5050]
  RGB_SMD_LED14 = SMD RGB LED (WS2812) [package=5050]
  RGB_SMD_LED15 = SMD RGB LED (WS2812) [package=5050]
  RGB_SMD_LED16 = SMD RGB LED (WS2812) [package=5050]
  RGB_SMD_LED17 = SMD RGB LED (WS2812) [package=5050]
  RGB_SMD_LED18 = SMD RGB LED (WS2812) [package=5050]
  RGB_SMD_LED19 = SMD RGB LED (WS2812) [package=5050]
  RGB_SMD_LED20 = SMD RGB LED (WS2812) [package=5050]
  RGB_SMD_LED21 = SMD RGB LED (WS2812) [package=5050]
  RGB_SMD_LED22 = SMD RGB LED (WS2812) [package=5050]
  RGB_SMD_LED23 = SMD RGB LED (WS2812) [package=5050]
  RGB_SMD_LED24 = SMD RGB LED (WS2812) [package=5050]
  RGB_SMD_LED25 = SMD RGB LED (WS2812) [package=5050]
  RGB_SMD_LED26 = SMD RGB LED (WS2812) [package=5050]
  RGB_SMD_LED27 = SMD RGB LED (WS2812) [package=5050]
  RGB_SMD_LED28 = SMD RGB LED (WS2812) [package=5050]
  RGB_SMD_LED29 = SMD RGB LED (WS2812) [package=5050]
  RGB_SMD_LED30 = SMD RGB LED (WS2812) [package=5050]
  RGB_SMD_LED31 = SMD RGB LED (WS2812) [package=5050]
  RGB_SMD_LED32 = SMD RGB LED (WS2812) [package=5050]
  RGB_SMD_LED33 = SMD RGB LED (WS2812) [package=5050]
  RGB_SMD_LED34 = SMD RGB LED (WS2812) [package=5050]
  RGB_SMD_LED35 = SMD RGB LED (WS2812) [package=5050]
  RGB_SMD_LED36 = SMD RGB LED (WS2812) [package=5050]
  RGB_SMD_LED37 = SMD RGB LED (WS2812) [package=5050]
  RGB_SMD_LED38 = SMD RGB LED (WS2812) [package=5050]
  RGB_SMD_LED39 = SMD RGB LED (WS2812) [package=5050]
  RGB_SMD_LED40 = SMD RGB LED (WS2812) [package=5050]
  RGB_SMD_LED41 = SMD RGB LED (WS2812) [package=5050]
  RGB_SMD_LED42 = SMD RGB LED (WS2812) [package=5050]
  RGB_SMD_LED43 = SMD RGB LED (WS2812) [package=5050]
  RGB_SMD_LED44 = SMD RGB LED (WS2812) [package=5050]
  RGB_SMD_LED45 = SMD RGB LED (WS2812) [package=5050]
  RGB_SMD_LED46 = SMD RGB LED (WS2812) [package=5050]
  RGB_SMD_LED47 = SMD RGB LED (WS2812) [package=5050]
  RGB_SMD_LED48 = SMD RGB LED (WS2812) [package=5050]
  RGB_SMD_LED49 = SMD RGB LED (WS2812) [package=5050]
  RGB_SMD_LED50 = SMD RGB LED (WS2812) [package=5050]
  RGB_SMD_LED51 = SMD RGB LED (WS2812) [package=5050]
  RGB_SMD_LED52 = SMD RGB LED (WS2812) [package=5050]
  RGB_SMD_LED53 = SMD RGB LED (WS2812) [package=5050]
  RGB_SMD_LED54 = SMD RGB LED (WS2812) [package=5050]
  RGB_SMD_LED55 = SMD RGB LED (WS2812) [package=5050]
  RGB_SMD_LED56 = SMD RGB LED (WS2812) [package=5050]
  RGB_SMD_LED57 = SMD RGB LED (WS2812) [package=5050]
  RGB_SMD_LED58 = SMD RGB LED (WS2812) [package=5050]
  RGB_SMD_LED59 = SMD RGB LED (WS2812) [package=5050]
  RGB_SMD_LED60 = SMD RGB LED (WS2812) [package=5050]
  RGB_SMD_LED61 = SMD RGB LED (WS2812) [package=5050]
  RGB_SMD_LED62 = SMD RGB LED (WS2812) [package=5050]
  RGB_SMD_LED63 = SMD RGB LED (WS2812) [package=5050]
  RGB_SMD_LED64 = SMD RGB LED (WS2812) [package=5050]
  RGB_SMD_LED65 = SMD RGB LED (WS2812) [package=5050]
  R18 = Resistor [tolerance=±5% resistance=220 package="2010 [SMD]"]  # not connected
  R19 = Resistor [tolerance=±5% resistance=220 package="2010 [SMD]"]  # not connected
  R20 = Resistor [tolerance=±5% resistance=220 package="2010 [SMD]"]  # not connected
  R21 = Resistor [tolerance=±5% resistance=220 package="2010 [SMD]"]  # not connected
  R22 = Resistor [tolerance=±5% resistance=220 package="2010 [SMD]"]  # not connected
  R23 = Resistor [tolerance=±5% resistance=220 package="2010 [SMD]"]  # not connected
  R24 = Resistor [tolerance=±5% resistance=220 package="2010 [SMD]"]  # not connected
  R25 = Resistor [tolerance=±5% resistance=220 package="2010 [SMD]"]  # not connected
  R26 = Resistor [tolerance=±5% resistance=220 package="2010 [SMD]"]  # not connected
  R27 = Resistor [tolerance=±5% resistance=220 package="2010 [SMD]"]  # not connected
  R28 = Resistor [tolerance=±5% resistance=220 package="2010 [SMD]"]  # not connected
  R29 = Resistor [tolerance=±5% resistance=220 package="2010 [SMD]"]  # not connected
  R30 = Resistor [tolerance=±5% resistance=220 package="2010 [SMD]"]  # not connected
  R31 = Resistor [tolerance=±5% resistance=220 package="2010 [SMD]"]  # not connected
  R32 = Resistor [tolerance=±5% resistance=220 package="2010 [SMD]"]  # not connected
  R33 = Resistor [tolerance=±5% resistance=220 package="2010 [SMD]"]  # not connected
  R34 = Resistor [tolerance=±5% resistance=220 package="2010 [SMD]"]  # not connected
  R35 = Resistor [tolerance=±5% resistance=220 package="2010 [SMD]"]  # not connected
  R36 = Resistor [tolerance=±5% resistance=220 package="2010 [SMD]"]  # not connected
  R37 = Resistor [tolerance=±5% resistance=220 package="2010 [SMD]"]  # not connected
  R38 = Resistor [tolerance=±5% resistance=220 package="2010 [SMD]"]  # not connected
  R39 = Resistor [tolerance=±5% resistance=220 package="2010 [SMD]"]  # not connected
  R40 = Resistor [tolerance=±5% resistance=220 package="2010 [SMD]"]  # not connected
  R41 = Resistor [tolerance=±5% resistance=220 package="2010 [SMD]"]  # not connected
  R42 = Resistor [tolerance=±5% resistance=220 package="2010 [SMD]"]  # not connected
  R43 = Resistor [tolerance=±5% resistance=220 package="2010 [SMD]"]  # not connected
  R44 = Resistor [tolerance=±5% resistance=220 package="2010 [SMD]"]  # not connected
  R45 = Resistor [tolerance=±5% resistance=220 package="2010 [SMD]"]  # not connected
  R46 = Resistor [tolerance=±5% resistance=220 package="2010 [SMD]"]  # not connected
  R47 = Resistor [tolerance=±5% resistance=220 package="2010 [SMD]"]  # not connected
  R48 = Resistor [tolerance=±5% resistance=220 package="2010 [SMD]"]  # not connected
  R49 = Resistor [tolerance=±5% resistance=220 package="2010 [SMD]"]  # not connected
  R50 = Resistor [tolerance=±5% resistance=220 package="2010 [SMD]"]  # not connected
  R51 = Resistor [tolerance=±5% resistance=220 package="2010 [SMD]"]  # not connected
  R52 = Resistor [tolerance=±5% resistance=220 package="2010 [SMD]"]  # not connected
  R53 = Resistor [tolerance=±5% resistance=220 package="2010 [SMD]"]  # not connected
  R54 = Resistor [tolerance=±5% resistance=220 package="2010 [SMD]"]  # not connected
  R55 = Resistor [tolerance=±5% resistance=220 package="2010 [SMD]"]  # not connected
  R56 = Resistor [tolerance=±5% resistance=220 package="2010 [SMD]"]  # not connected
  R57 = Resistor [tolerance=±5% resistance=220 package="2010 [SMD]"]  # not connected
  R58 = Resistor [tolerance=±5% resistance=220 package="2010 [SMD]"]  # not connected
  R59 = Resistor [tolerance=±5% resistance=220 package="2010 [SMD]"]  # not connected
  R60 = Resistor [tolerance=±5% resistance=220 package="2010 [SMD]"]  # not connected
  R61 = Resistor [tolerance=±5% resistance=220 package="2010 [SMD]"]  # not connected
  R62 = Resistor [tolerance=±5% resistance=220 package="2010 [SMD]"]  # not connected
  R63 = Resistor [tolerance=±5% resistance=220 package="2010 [SMD]"]  # not connected
  R64 = Resistor [tolerance=±5% resistance=220 package="2010 [SMD]"]  # not connected
  R65 = Resistor [tolerance=±5% resistance=220 package="2010 [SMD]"]  # not connected
  R66 = Resistor [tolerance=±5% resistance=220 package="2010 [SMD]"]  # not connected
  R67 = Resistor [tolerance=±5% resistance=220 package="2010 [SMD]"]  # not connected
  R68 = Resistor [tolerance=±5% resistance=220 package="2010 [SMD]"]  # not connected
  R69 = Resistor [tolerance=±5% resistance=220 package="2010 [SMD]"]  # not connected
  R70 = Resistor [tolerance=±5% resistance=220 package="2010 [SMD]"]  # not connected
  R71 = Resistor [tolerance=±5% resistance=220 package="2010 [SMD]"]  # not connected
  R72 = Resistor [tolerance=±5% resistance=220 package="2010 [SMD]"]  # not connected
  R73 = Resistor [tolerance=±5% resistance=220 package="2010 [SMD]"]  # not connected
  Part10 = Shift Register Breakout - 74HC595
  R74 = Resistor [tolerance=±5% resistance=220 package="0805 [SMD]"]  # not connected
  R75 = Resistor [tolerance=±5% resistance=220 package="0805 [SMD]"]  # not connected
  R76 = Resistor [tolerance=±5% resistance=220 package="0805 [SMD]"]  # not connected
  R77 = Resistor [tolerance=±5% resistance=220 package="0805 [SMD]"]  # not connected
  R78 = Resistor [tolerance=±5% resistance=220 package="0805 [SMD]"]  # not connected
  R79 = Resistor [tolerance=±5% resistance=220 package="0805 [SMD]"]  # not connected
  R80 = Resistor [tolerance=±5% resistance=220 package="0805 [SMD]"]  # not connected
  R81 = Resistor [tolerance=±5% resistance=220 package="0805 [SMD]"]  # not connected
  S65 = Round Pushbutton  # not connected
  S66 = Round Pushbutton  # not connected
  S67 = Round Pushbutton  # not connected
  S68 = Round Pushbutton  # not connected
  S69 = Toggle Switch [package=THT]  # not connected
  S70 = Toggle Switch [package=THT]
  S71 = Toggle Switch [package=THT]  # not connected
  S72 = Toggle Switch [package=THT]  # not connected
  LED1 = smd LED [color="Green (560nm)" package="1206 [SMD]"]
  LED2 = smd LED [color="Green (565nm)" package="1206 [SMD]"]
  R82 = Resistor [tolerance=±5% resistance=220 package="0805 [SMD]"]
  R83 = Resistor [tolerance=±5% resistance=220 package="0805 [SMD]"]

nets:
  N1: C1.+, J1.PWR, S70.COM
  N2: C1.-, J1.GND, RGB_SMD_LED1.DOut, S70.L1, LED1.cathode, LED2.cathode
  N3: R1.Pin_1, RGB_SMD_LED1.DIn
  N4: RGB_SMD_LED1.VCC, S70.L2, R82.Pin_0
  N5: RGB_SMD_LED1.NC, RGB_SMD_LED9.VCC
  N6: RGB_SMD_LED1.VDD, RGB_SMD_LED9.DIn
  N7: RGB_SMD_LED1.VSS, RGB_SMD_LED9.DOut
  N8: S1.pin_1, S2.pin_1, S3.pin_1, S4.pin_1, S5.pin_1, S6.pin_1, S7.pin_1, S8.pin_1, S9.pin_1, S10.pin_1, S11.pin_1, S12.pin_1, S13.pin_1, S14.pin_1, S15.pin_1, S16.pin_1, S17.pin_1, S18.pin_1, S19.pin_1, S20.pin_1, S21.pin_1, S22.pin_1, S23.pin_1, S24.pin_1, S25.pin_1, S26.pin_1, S27.pin_1, S28.pin_1, S29.pin_1, S30.pin_1, S31.pin_1, S32.pin_1, S33.pin_1, S34.pin_1, S35.pin_1, S36.pin_1, S37.pin_1, S38.pin_1, S39.pin_1, S40.pin_1, S41.pin_1, S42.pin_1, S43.pin_1, S44.pin_1, S45.pin_1, S46.pin_1, S47.pin_1, S48.pin_1, S49.pin_1, S50.pin_1, S51.pin_1, S52.pin_1, S53.pin_1, S54.pin_1, S55.pin_1, S56.pin_1, S57.pin_1, S58.pin_1, S59.pin_1, S60.pin_1, S61.pin_1, S62.pin_1, S63.pin_1, S64.pin_1
  VCC: Part2.VCC, Part3.VCC, Part4.VCC, Part5.VCC, Part6.VCC, Part7.VCC, Part8.VCC, Part9.VCC, Part10.VCC
  GND: Part2.GND, Part3.GND, Part4.GND, Part5.GND, Part6.GND, Part7.GND, Part8.GND, Part9.GND, Part10.GND
  N9: Part2./OUTPUT_ENABLE, Part3./OUTPUT_ENABLE, Part4./OUTPUT_ENABLE, Part5./OUTPUT_ENABLE, Part6./OUTPUT_ENABLE, Part7./OUTPUT_ENABLE, Part8./OUTPUT_ENABLE, Part9./OUTPUT_ENABLE, Part10./OUTPUT_ENABLE
  N10: Part2.CLOCK, Part3.CLOCK, Part4.CLOCK, Part5.CLOCK, Part6.CLOCK, Part7.CLOCK, Part8.CLOCK, Part9.CLOCK, Part10.CLOCK
  N11: Part2.LATCH_CLOCK, Part3.LATCH_CLOCK, Part4.LATCH_CLOCK, Part5.LATCH_CLOCK, Part6.LATCH_CLOCK, Part7.LATCH_CLOCK, Part8.LATCH_CLOCK, Part9.LATCH_CLOCK, Part10.LATCH_CLOCK
  N12: Part2.SERIAL_IN, Part3.SERIAL_OUT
  N13: Part3.SERIAL_IN, Part4.SERIAL_OUT
  N14: Part4.SERIAL_IN, Part5.SERIAL_OUT
  N15: Part5.SERIAL_IN, Part6.SERIAL_OUT
  N16: Part6.SERIAL_IN, Part7.SERIAL_OUT
  N17: Part7.SERIAL_IN, Part8.SERIAL_OUT
  N18: Part8.SERIAL_IN, Part9.SERIAL_OUT
  N19: Part9.SERIAL_IN, Part10.SERIAL_OUT
  N20: RGB_SMD_LED2.DOut, RGB_SMD_LED5.VSS
  N21: RGB_SMD_LED2.DIn, RGB_SMD_LED5.VDD
  N22: RGB_SMD_LED2.VCC, RGB_SMD_LED5.NC
  N23: RGB_SMD_LED2.NC, RGB_SMD_LED3.VCC
  N24: RGB_SMD_LED2.VDD, RGB_SMD_LED3.DIn
  N25: RGB_SMD_LED2.VSS, RGB_SMD_LED3.DOut
  N26: RGB_SMD_LED3.NC, RGB_SMD_LED4.VCC
  N27: RGB_SMD_LED3.VDD, RGB_SMD_LED4.DIn
  N28: RGB_SMD_LED3.VSS, RGB_SMD_LED4.DOut
  N29: RGB_SMD_LED4.NC, RGB_SMD_LED13.VCC
  N30: RGB_SMD_LED4.VDD, RGB_SMD_LED13.DIn
  N31: RGB_SMD_LED4.VSS, RGB_SMD_LED13.DOut
  N32: RGB_SMD_LED5.DOut, RGB_SMD_LED7.VSS
  N33: RGB_SMD_LED5.DIn, RGB_SMD_LED7.VDD
  N34: RGB_SMD_LED5.VCC, RGB_SMD_LED7.NC
  N35: RGB_SMD_LED7.DOut, RGB_SMD_LED8.VSS
  N36: RGB_SMD_LED7.DIn, RGB_SMD_LED8.VDD
  N37: RGB_SMD_LED7.VCC, RGB_SMD_LED8.NC
  N38: RGB_SMD_LED8.DOut, RGB_SMD_LED9.VSS
  N39: RGB_SMD_LED8.DIn, RGB_SMD_LED9.VDD
  N40: RGB_SMD_LED8.VCC, RGB_SMD_LED9.NC
  N41: RGB_SMD_LED10.DOut, RGB_SMD_LED14.VSS
  N42: RGB_SMD_LED10.DIn, RGB_SMD_LED14.VDD
  N43: RGB_SMD_LED10.VCC, RGB_SMD_LED14.NC
  N44: RGB_SMD_LED10.NC, RGB_SMD_LED16.VCC
  N45: RGB_SMD_LED10.VDD, RGB_SMD_LED16.DIn
  N46: RGB_SMD_LED10.VSS, RGB_SMD_LED16.DOut
  N47: RGB_SMD_LED11.DOut, RGB_SMD_LED15.VSS
  N48: RGB_SMD_LED11.DIn, RGB_SMD_LED15.VDD
  N49: RGB_SMD_LED11.VCC, RGB_SMD_LED15.NC
  N50: RGB_SMD_LED11.NC, RGB_SMD_LED14.VCC
  N51: RGB_SMD_LED11.VDD, RGB_SMD_LED14.DIn
  N52: RGB_SMD_LED11.VSS, RGB_SMD_LED14.DOut
  N53: RGB_SMD_LED12.DOut, RGB_SMD_LED17.VSS
  N54: RGB_SMD_LED12.DIn, RGB_SMD_LED17.VDD
  N55: RGB_SMD_LED12.VCC, RGB_SMD_LED17.NC
  N56: RGB_SMD_LED12.NC, RGB_SMD_LED21.VCC
  N57: RGB_SMD_LED12.VDD, RGB_SMD_LED21.DIn
  N58: RGB_SMD_LED12.VSS, RGB_SMD_LED21.DOut
  N59: RGB_SMD_LED13.NC, RGB_SMD_LED15.VCC
  N60: RGB_SMD_LED13.VDD, RGB_SMD_LED15.DIn
  N61: RGB_SMD_LED13.VSS, RGB_SMD_LED15.DOut
  N62: RGB_SMD_LED16.NC, RGB_SMD_LED17.VCC
  N63: RGB_SMD_LED16.VDD, RGB_SMD_LED17.DIn
  N64: RGB_SMD_LED16.VSS, RGB_SMD_LED17.DOut
  N65: RGB_SMD_LED18.DOut, RGB_SMD_LED22.VSS
  N66: RGB_SMD_LED18.DIn, RGB_SMD_LED22.VDD
  N67: RGB_SMD_LED18.VCC, RGB_SMD_LED22.NC
  N68: RGB_SMD_LED18.NC, RGB_SMD_LED24.VCC
  N69: RGB_SMD_LED18.VDD, RGB_SMD_LED24.DIn
  N70: RGB_SMD_LED18.VSS, RGB_SMD_LED24.DOut
  N71: RGB_SMD_LED19.DOut, RGB_SMD_LED23.VSS
  N72: RGB_SMD_LED19.DIn, RGB_SMD_LED23.VDD
  N73: RGB_SMD_LED19.VCC, RGB_SMD_LED23.NC
  N74: RGB_SMD_LED19.NC, RGB_SMD_LED22.VCC
  N75: RGB_SMD_LED19.VDD, RGB_SMD_LED22.DIn
  N76: RGB_SMD_LED19.VSS, RGB_SMD_LED22.DOut
  N77: RGB_SMD_LED20.DOut, RGB_SMD_LED25.VSS
  N78: RGB_SMD_LED20.DIn, RGB_SMD_LED25.VDD
  N79: RGB_SMD_LED20.VCC, RGB_SMD_LED25.NC
  N80: RGB_SMD_LED20.NC, RGB_SMD_LED29.VCC
  N81: RGB_SMD_LED20.VDD, RGB_SMD_LED29.DIn
  N82: RGB_SMD_LED20.VSS, RGB_SMD_LED29.DOut
  N83: RGB_SMD_LED21.NC, RGB_SMD_LED23.VCC
  N84: RGB_SMD_LED21.VDD, RGB_SMD_LED23.DIn
  N85: RGB_SMD_LED21.VSS, RGB_SMD_LED23.DOut
  N86: RGB_SMD_LED24.NC, RGB_SMD_LED25.VCC
  N87: RGB_SMD_LED24.VDD, RGB_SMD_LED25.DIn
  N88: RGB_SMD_LED24.VSS, RGB_SMD_LED25.DOut
  N89: RGB_SMD_LED26.DOut, RGB_SMD_LED30.VSS
  N90: RGB_SMD_LED26.DIn, RGB_SMD_LED30.VDD
  N91: RGB_SMD_LED26.VCC, RGB_SMD_LED30.NC
  N92: RGB_SMD_LED26.NC, RGB_SMD_LED32.VCC
  N93: RGB_SMD_LED26.VDD, RGB_SMD_LED32.DIn
  N94: RGB_SMD_LED26.VSS, RGB_SMD_LED32.DOut
  N95: RGB_SMD_LED27.DOut, RGB_SMD_LED31.VSS
  N96: RGB_SMD_LED27.DIn, RGB_SMD_LED31.VDD
  N97: RGB_SMD_LED27.VCC, RGB_SMD_LED31.NC
  N98: RGB_SMD_LED27.NC, RGB_SMD_LED30.VCC
  N99: RGB_SMD_LED27.VDD, RGB_SMD_LED30.DIn
  N100: RGB_SMD_LED27.VSS, RGB_SMD_LED30.DOut
  N101: RGB_SMD_LED28.DOut, RGB_SMD_LED33.VSS
  N102: RGB_SMD_LED28.DIn, RGB_SMD_LED33.VDD
  N103: RGB_SMD_LED28.VCC, RGB_SMD_LED33.NC
  N104: RGB_SMD_LED28.NC, RGB_SMD_LED37.VCC
  N105: RGB_SMD_LED28.VDD, RGB_SMD_LED37.DIn
  N106: RGB_SMD_LED28.VSS, RGB_SMD_LED37.DOut
  N107: RGB_SMD_LED29.NC, RGB_SMD_LED31.VCC
  N108: RGB_SMD_LED29.VDD, RGB_SMD_LED31.DIn
  N109: RGB_SMD_LED29.VSS, RGB_SMD_LED31.DOut
  N110: RGB_SMD_LED32.NC, RGB_SMD_LED33.VCC
  N111: RGB_SMD_LED32.VDD, RGB_SMD_LED33.DIn
  N112: RGB_SMD_LED32.VSS, RGB_SMD_LED33.DOut
  N113: RGB_SMD_LED34.DOut, RGB_SMD_LED38.VSS
  N114: RGB_SMD_LED34.DIn, RGB_SMD_LED38.VDD
  N115: RGB_SMD_LED34.VCC, RGB_SMD_LED38.NC
  N116: RGB_SMD_LED34.NC, RGB_SMD_LED40.VCC
  N117: RGB_SMD_LED34.VDD, RGB_SMD_LED40.DIn
  N118: RGB_SMD_LED34.VSS, RGB_SMD_LED40.DOut
  N119: RGB_SMD_LED35.DOut, RGB_SMD_LED39.VSS
  N120: RGB_SMD_LED35.DIn, RGB_SMD_LED39.VDD
  N121: RGB_SMD_LED35.VCC, RGB_SMD_LED39.NC
  N122: RGB_SMD_LED35.NC, RGB_SMD_LED38.VCC
  N123: RGB_SMD_LED35.VDD, RGB_SMD_LED38.DIn
  N124: RGB_SMD_LED35.VSS, RGB_SMD_LED38.DOut
  N125: RGB_SMD_LED36.DOut, RGB_SMD_LED41.VSS
  N126: RGB_SMD_LED36.DIn, RGB_SMD_LED41.VDD
  N127: RGB_SMD_LED36.VCC, RGB_SMD_LED41.NC
  N128: RGB_SMD_LED36.NC, RGB_SMD_LED45.VCC
  N129: RGB_SMD_LED36.VDD, RGB_SMD_LED45.DIn
  N130: RGB_SMD_LED36.VSS, RGB_SMD_LED45.DOut
  N131: RGB_SMD_LED37.NC, RGB_SMD_LED39.VCC
  N132: RGB_SMD_LED37.VDD, RGB_SMD_LED39.DIn
  N133: RGB_SMD_LED37.VSS, RGB_SMD_LED39.DOut
  N134: RGB_SMD_LED40.NC, RGB_SMD_LED41.VCC
  N135: RGB_SMD_LED40.VDD, RGB_SMD_LED41.DIn
  N136: RGB_SMD_LED40.VSS, RGB_SMD_LED41.DOut
  N137: RGB_SMD_LED42.DOut, RGB_SMD_LED46.VSS
  N138: RGB_SMD_LED42.DIn, RGB_SMD_LED46.VDD
  N139: RGB_SMD_LED42.VCC, RGB_SMD_LED46.NC
  N140: RGB_SMD_LED42.NC, RGB_SMD_LED48.VCC
  N141: RGB_SMD_LED42.VDD, RGB_SMD_LED48.DIn
  N142: RGB_SMD_LED42.VSS, RGB_SMD_LED48.DOut
  N143: RGB_SMD_LED43.DOut, RGB_SMD_LED47.VSS
  N144: RGB_SMD_LED43.DIn, RGB_SMD_LED47.VDD
  N145: RGB_SMD_LED43.VCC, RGB_SMD_LED47.NC
  N146: RGB_SMD_LED43.NC, RGB_SMD_LED46.VCC
  N147: RGB_SMD_LED43.VDD, RGB_SMD_LED46.DIn
  N148: RGB_SMD_LED43.VSS, RGB_SMD_LED46.DOut
  N149: RGB_SMD_LED44.DOut, RGB_SMD_LED49.VSS
  N150: RGB_SMD_LED44.DIn, RGB_SMD_LED49.VDD
  N151: RGB_SMD_LED44.VCC, RGB_SMD_LED49.NC
  N152: RGB_SMD_LED44.NC, RGB_SMD_LED53.VCC
  N153: RGB_SMD_LED44.VDD, RGB_SMD_LED53.DIn
  N154: RGB_SMD_LED44.VSS, RGB_SMD_LED53.DOut
  N155: RGB_SMD_LED45.NC, RGB_SMD_LED47.VCC
  N156: RGB_SMD_LED45.VDD, RGB_SMD_LED47.DIn
  N157: RGB_SMD_LED45.VSS, RGB_SMD_LED47.DOut
  N158: RGB_SMD_LED48.NC, RGB_SMD_LED49.VCC
  N159: RGB_SMD_LED48.VDD, RGB_SMD_LED49.DIn
  N160: RGB_SMD_LED48.VSS, RGB_SMD_LED49.DOut
  N161: RGB_SMD_LED50.DOut, RGB_SMD_LED54.VSS
  N162: RGB_SMD_LED50.DIn, RGB_SMD_LED54.VDD
  N163: RGB_SMD_LED50.VCC, RGB_SMD_LED54.NC
  N164: RGB_SMD_LED50.NC, RGB_SMD_LED56.VCC
  N165: RGB_SMD_LED50.VDD, RGB_SMD_LED56.DIn
  N166: RGB_SMD_LED50.VSS, RGB_SMD_LED56.DOut
  N167: RGB_SMD_LED51.DOut, RGB_SMD_LED55.VSS
  N168: RGB_SMD_LED51.DIn, RGB_SMD_LED55.VDD
  N169: RGB_SMD_LED51.VCC, RGB_SMD_LED55.NC
  N170: RGB_SMD_LED51.NC, RGB_SMD_LED54.VCC
  N171: RGB_SMD_LED51.VDD, RGB_SMD_LED54.DIn
  N172: RGB_SMD_LED51.VSS, RGB_SMD_LED54.DOut
  N173: RGB_SMD_LED52.DOut, RGB_SMD_LED57.VSS
  N174: RGB_SMD_LED52.DIn, RGB_SMD_LED57.VDD
  N175: RGB_SMD_LED52.VCC, RGB_SMD_LED57.NC
  N176: RGB_SMD_LED52.NC, RGB_SMD_LED61.VCC
  N177: RGB_SMD_LED52.VDD, RGB_SMD_LED61.DIn
  N178: RGB_SMD_LED52.VSS, RGB_SMD_LED61.DOut
  N179: RGB_SMD_LED53.NC, RGB_SMD_LED55.VCC
  N180: RGB_SMD_LED53.VDD, RGB_SMD_LED55.DIn
  N181: RGB_SMD_LED53.VSS, RGB_SMD_LED55.DOut
  N182: RGB_SMD_LED56.NC, RGB_SMD_LED57.VCC
  N183: RGB_SMD_LED56.VDD, RGB_SMD_LED57.DIn
  N184: RGB_SMD_LED56.VSS, RGB_SMD_LED57.DOut
  N185: RGB_SMD_LED58.DOut, RGB_SMD_LED62.VSS
  N186: RGB_SMD_LED58.DIn, RGB_SMD_LED62.VDD
  N187: RGB_SMD_LED58.VCC, RGB_SMD_LED62.NC
  N188: RGB_SMD_LED58.NC, RGB_SMD_LED64.VCC
  N189: RGB_SMD_LED58.VDD, RGB_SMD_LED64.DIn
  N190: RGB_SMD_LED58.VSS, RGB_SMD_LED64.DOut
  N191: RGB_SMD_LED59.DOut, RGB_SMD_LED63.VSS
  N192: RGB_SMD_LED59.DIn, RGB_SMD_LED63.VDD
  N193: RGB_SMD_LED59.VCC, RGB_SMD_LED63.NC
  N194: RGB_SMD_LED59.NC, RGB_SMD_LED62.VCC
  N195: RGB_SMD_LED59.VDD, RGB_SMD_LED62.DIn
  N196: RGB_SMD_LED59.VSS, RGB_SMD_LED62.DOut
  N197: RGB_SMD_LED60.DOut, RGB_SMD_LED65.VSS
  N198: RGB_SMD_LED60.DIn, RGB_SMD_LED65.VDD
  N199: RGB_SMD_LED60.VCC, RGB_SMD_LED65.NC
  N200: RGB_SMD_LED61.NC, RGB_SMD_LED63.VCC
  N201: RGB_SMD_LED61.VDD, RGB_SMD_LED63.DIn
  N202: RGB_SMD_LED61.VSS, RGB_SMD_LED63.DOut
  N203: RGB_SMD_LED64.NC, RGB_SMD_LED65.VCC
  N204: RGB_SMD_LED64.VDD, RGB_SMD_LED65.DIn
  N205: RGB_SMD_LED64.VSS, RGB_SMD_LED65.DOut
  N206: LED1.anode, R82.Pin_1
  N207: LED2.anode, R83.Pin_0

notes:
  Power switch
  On Off
  LED switch
  Off On
  Side switch
  Black(low) White(high)
  Enter button
  Draw button
  Concede button
  Castle button
  Castle side switch
  Queen(low) King(high)
  The Ws2812 LED breakouts here are not the ones I used. The ones I used have VCC, Din, and GND on one side, and VCC, Do, and GRN on the other, I have wired them here like they are those LED breakouts.
  Pins on the ESP8266 Sparkfun Thing Dev Board are as follows:
  Pin 0: clockpin on shift in register
  Pin 2: ploadpin on shift in register
  Pin 5: Din of WS2812 string
  Pin 4: dataPin on shift in register
  Pin 12: RX of LCD screen
  Pin 13: clock enable pin of shift in register
  Pin 14: Side switch
  GND: Ground
  VIN: High
  I used SN74HC165 Shift-in registers instead of shift out pictured here, but I have wired them as if they were shift in registers.
